// Logisim project 4bitcpu.circ as structural Verilog: 4 circuits, main circuit fourbitadder
module fourbitadder (
  input  Carry_In,
  input  B1,
  input  B2,
  input  B3,
  input  B4,
  input  A1,
  input  A2,
  input  A3,
  input  A4,
  output O1,
  output O2,
  output O3,
  output O4,
  output Overflow
);

  wire and_1_out, and_2_out, and_3_out, and_4_out, and_5_out, and_6_out, and_7_out, and_8_out, or_2_out,
       or_3_out, or_4_out, xor_1_out, xor_2_out, xor_3_out, xor_4_out;

  and and_1 (and_1_out, B4, A4);
  xor xor_1 (xor_1_out, A4, B4);
  and and_2 (and_2_out, B3, A3);
  xor xor_2 (xor_2_out, A3, B3);
  and and_3 (and_3_out, B2, A2);
  xor xor_3 (xor_3_out, A2, B2);
  and and_4 (and_4_out, B1, A1);
  xor xor_4 (xor_4_out, A1, B1);
  and and_5 (and_5_out, or_2_out, xor_1_out);
  xor xor_5 (O4, xor_1_out, or_2_out);
  and and_6 (and_6_out, or_3_out, xor_2_out);
  xor xor_6 (O3, xor_2_out, or_3_out);
  and and_7 (and_7_out, or_4_out, xor_3_out);
  xor xor_7 (O2, xor_3_out, or_4_out);
  and and_8 (and_8_out, Carry_In, xor_4_out);
  xor xor_8 (O1, xor_4_out, Carry_In);
  or or_1 (Overflow, and_5_out, and_1_out);
  or or_2 (or_2_out, and_6_out, and_2_out);
  or or_3 (or_3_out, and_7_out, and_3_out);
  or or_4 (or_4_out, and_8_out, and_4_out);
endmodule

module cpu (
  input  in_1,
  input  in_2,
  input  in_3,
  input  in_4,
  input  Clock,
  input  Store_A,
  input  Store_B,
  input  STORE_R,
  input  Write_A,
  input  Write_B,
  input  Write_R,
  input  Write_Mem,
  input  LDAM,
  input  LDAB,
  input  LDAR,
  input  LDBM,
  input  LDBA,
  input  LDBR,
  input  [7:0] in_19,
  input  in_20,
  input  in_21,
  input  [7:0] in_22
);

  wire ADD_o1, ADD_o2, ADD_o3, ADD_o4, controlled_buffer_1_out, controlled_buffer_2_out,
       controlled_buffer_3_out, controlled_buffer_4_out, controlled_buffer_5_out, Register_A_stored_1,
       Register_A_stored_2, Register_A_stored_3, Register_A_stored_4, Register_B_stored_1,
       Register_B_stored_2, Register_B_stored_3, Register_B_stored_4, Register_Result_stored_1,
       Register_Result_stored_2, Register_Result_stored_3, Register_Result_stored_4, undriven, undriven_2;
  wire [7:0] undriven_3;

  assign controlled_buffer_1_out = controlled_buffer_5_out ? in_1 : 1'bz;  // Controlled_Buffer controlled_buffer_1
  assign controlled_buffer_2_out = controlled_buffer_5_out ? in_2 : 1'bz;  // Controlled_Buffer controlled_buffer_2
  assign controlled_buffer_3_out = controlled_buffer_5_out ? in_3 : 1'bz;  // Controlled_Buffer controlled_buffer_3
  assign controlled_buffer_4_out = controlled_buffer_5_out ? in_4 : 1'bz;  // Controlled_Buffer controlled_buffer_4
  assign controlled_buffer_5_out = LDAM ? LDAM : 1'bz;  // Controlled_Buffer controlled_buffer_5
  assign controlled_buffer_5_out = LDAB ? LDAB : 1'bz;  // Controlled_Buffer controlled_buffer_6
  assign controlled_buffer_5_out = LDAR ? LDAR : 1'bz;  // Controlled_Buffer controlled_buffer_7
  assign controlled_buffer_5_out = LDBM ? LDBM : 1'bz;  // Controlled_Buffer controlled_buffer_8
  assign controlled_buffer_1_out = controlled_buffer_5_out ? Register_A_stored_1 : 1'bz;  // Controlled_Buffer controlled_buffer_9
  assign controlled_buffer_2_out = controlled_buffer_5_out ? Register_A_stored_2 : 1'bz;  // Controlled_Buffer controlled_buffer_10
  fourbitreg Register_A (
    .DATA1(controlled_buffer_1_out), .DATA2(controlled_buffer_2_out), .DATA3(controlled_buffer_3_out),
    .DATA4(controlled_buffer_4_out), .S(controlled_buffer_5_out), .C(undriven_2),
    .Stored_1(Register_A_stored_1), .Stored_2(Register_A_stored_2), .Stored_3(Register_A_stored_3),
    .Stored_4(Register_A_stored_4));
  assign controlled_buffer_5_out = LDBA ? LDBA : 1'bz;  // Controlled_Buffer controlled_buffer_11
  assign controlled_buffer_5_out = LDBR ? LDBR : 1'bz;  // Controlled_Buffer controlled_buffer_12
  assign controlled_buffer_3_out = controlled_buffer_5_out ? Register_A_stored_3 : 1'bz;  // Controlled_Buffer controlled_buffer_13
  assign controlled_buffer_4_out = controlled_buffer_5_out ? Register_A_stored_4 : 1'bz;  // Controlled_Buffer controlled_buffer_14
  fourbitreg Register_B (
    .DATA1(controlled_buffer_1_out), .DATA2(controlled_buffer_2_out), .DATA3(controlled_buffer_3_out),
    .DATA4(controlled_buffer_4_out), .S(controlled_buffer_5_out), .C(undriven_2),
    .Stored_1(Register_B_stored_1), .Stored_2(Register_B_stored_2), .Stored_3(Register_B_stored_3),
    .Stored_4(Register_B_stored_4));
  assign controlled_buffer_1_out = controlled_buffer_5_out ? Register_B_stored_1 : 1'bz;  // Controlled_Buffer controlled_buffer_15
  assign controlled_buffer_2_out = controlled_buffer_5_out ? Register_B_stored_2 : 1'bz;  // Controlled_Buffer controlled_buffer_16
  assign controlled_buffer_3_out = controlled_buffer_5_out ? Register_B_stored_3 : 1'bz;  // Controlled_Buffer controlled_buffer_17
  assign controlled_buffer_4_out = controlled_buffer_5_out ? Register_B_stored_4 : 1'bz;  // Controlled_Buffer controlled_buffer_18
  RAM ram_1 (.addr(in_19), .oe(in_20), .clk(in_21), .dout(in_22));  // open: we, din
  fourbitadder ADD (
    .B1(Register_B_stored_1), .B2(Register_B_stored_2), .B3(Register_B_stored_3), .B4(Register_B_stored_4),
    .A1(Register_A_stored_1), .A2(Register_A_stored_2), .A3(Register_A_stored_3), .A4(Register_A_stored_4),
    .O1(ADD_o1), .O2(ADD_o2), .O3(ADD_o3), .O4(ADD_o4));  // open: Carry_In, Overflow
  assign controlled_buffer_1_out = controlled_buffer_5_out ? Register_Result_stored_1 : 1'bz;  // Controlled_Buffer controlled_buffer_19
  fourbitreg Register_Result (
    .DATA1(ADD_o1), .DATA2(ADD_o2), .DATA3(ADD_o3), .DATA4(ADD_o4), .S(undriven), .C(undriven_2),
    .Stored_1(Register_Result_stored_1), .Stored_2(Register_Result_stored_2),
    .Stored_3(Register_Result_stored_3), .Stored_4(Register_Result_stored_4));
  assign controlled_buffer_2_out = controlled_buffer_5_out ? Register_Result_stored_2 : 1'bz;  // Controlled_Buffer controlled_buffer_20
  assign controlled_buffer_3_out = controlled_buffer_5_out ? Register_Result_stored_3 : 1'bz;  // Controlled_Buffer controlled_buffer_21
  assign controlled_buffer_4_out = controlled_buffer_5_out ? Register_Result_stored_4 : 1'bz;  // Controlled_Buffer controlled_buffer_22
  assign controlled_buffer_1_out = controlled_buffer_5_out ? undriven_3[0] : 1'bz;  // Controlled_Buffer controlled_buffer_23
  assign controlled_buffer_2_out = controlled_buffer_5_out ? undriven_3[1] : 1'bz;  // Controlled_Buffer controlled_buffer_24
  assign controlled_buffer_3_out = controlled_buffer_5_out ? undriven_3[2] : 1'bz;  // Controlled_Buffer controlled_buffer_25
  assign controlled_buffer_4_out = controlled_buffer_5_out ? undriven_3[3] : 1'bz;  // Controlled_Buffer controlled_buffer_26
  RAM ram_2 (.addr(undriven_3), .we(controlled_buffer_5_out), .clk(undriven_2));  // open: oe, din, dout
endmodule

module fourbitreg (
  input  DATA1,
  input  DATA2,
  input  DATA3,
  input  DATA4,
  input  S,
  input  C,
  output Stored_1,
  output Stored_2,
  output Stored_3,
  output Stored_4
);

  wire and_1_out, and_2_out, and_3_out, and_4_out, and_5_out, and_6_out, and_7_out, and_8_out, and_9_out,
       and_10_out, and_11_out, and_12_out, nor_1_out, nor_3_out, nor_5_out, nor_7_out, not_1_out, not_2_out,
       not_3_out, not_4_out;

  and and_1 (and_1_out, S, C);
  and and_2 (and_2_out, S, C);
  and and_3 (and_3_out, S, C);
  not not_1 (not_1_out, DATA4);
  and and_4 (and_4_out, S, C);
  and and_5 (and_5_out, DATA1, and_1_out);
  not not_2 (not_2_out, DATA1);
  and and_6 (and_6_out, not_2_out, and_1_out);
  and and_7 (and_7_out, DATA2, and_2_out);
  not not_3 (not_3_out, DATA2);
  and and_8 (and_8_out, not_3_out, and_2_out);
  and and_9 (and_9_out, DATA3, and_3_out);
  not not_4 (not_4_out, DATA3);
  and and_10 (and_10_out, not_4_out, and_3_out);
  and and_11 (and_11_out, DATA4, and_4_out);
  and and_12 (and_12_out, not_1_out, and_4_out);
  nor nor_1 (nor_1_out, and_5_out, Stored_1);
  nor nor_2 (Stored_1, nor_1_out, and_6_out);
  nor nor_3 (nor_3_out, and_7_out, Stored_2);
  nor nor_4 (Stored_2, nor_3_out, and_8_out);
  nor nor_5 (nor_5_out, and_9_out, Stored_3);
  nor nor_6 (Stored_3, nor_5_out, and_10_out);
  nor nor_7 (nor_7_out, and_11_out, Stored_4);
  nor nor_8 (Stored_4, nor_7_out, and_12_out);
endmodule

module fourbitmux (
  input  A1,
  input  A2,
  input  A3,
  input  A4,
  input  B1,
  input  B2,
  input  B3,
  input  B4,
  input  Switch,
  output O1,
  output O2,
  output O3,
  output O4
);

  wire and_1_out, and_2_out, and_3_out, and_4_out, and_5_out, and_6_out, and_7_out, and_8_out, not_1_out,
       not_2_out, not_3_out, not_4_out, not_5_out;

  not not_1 (not_1_out, Switch);
  not not_2 (not_2_out, not_1_out);
  not not_3 (not_3_out, not_1_out);
  not not_4 (not_4_out, not_1_out);
  not not_5 (not_5_out, not_1_out);
  and and_1 (and_1_out, A1, not_1_out);
  and and_2 (and_2_out, B1, not_2_out);
  and and_3 (and_3_out, A2, not_1_out);
  and and_4 (and_4_out, B2, not_3_out);
  and and_5 (and_5_out, A3, not_1_out);
  and and_6 (and_6_out, B3, not_4_out);
  and and_7 (and_7_out, A4, not_1_out);
  and and_8 (and_8_out, B4, not_5_out);
  or or_1 (O1, and_1_out, and_2_out);
  or or_2 (O2, and_3_out, and_4_out);
  or or_3 (O3, and_5_out, and_6_out);
  or or_4 (O4, and_7_out, and_8_out);
endmodule
